// Logisim project Project2.circ as structural Verilog: 11 circuits, main circuit MIPS32
module MIPS32 (
  input  [31:0] in_1,
  input  in_2,
  input  in_3,
  input  in_4,
  input  in_5,
  input  in_6,
  output [31:0] out_7
);

  wire clock_1_out, ctrlidex_1_com, ctrlidex_1_imm, ctrlidex_1_su, not_1_out, or_1_out, registerfile_1_p3;
  wire [1:0] forward_1_forwarda, forward_1_forwardb;
  wire [3:0] ctrlidex_1_alu;
  wire [4:0] ctrlexmem_1_dest, decode_1_ra, decode_1_rb, decode_1_shamt, idex_1_sa, registerfile_1_p4;
  wire [31:0] bit_extender_1_out, compare_1_o, ctrlexmem_1_q, ctrlidex_1_ctrl, D_q, idex_1_qa, idex_1_qb,
       idex_1_qimm, incrementer4_1_out_2, mips_alu_1_p5, multiplexer_1_out, multiplexer_2_out,
       multiplexer_3_out, multiplexer_4_out, multiplexer_5_out, pc_1_o, registerfile_1_p1, registerfile_1_p7,
       registerfile_1_p8;

  PC pc_1 (.I(incrementer4_1_out_2), .Reset(in_2), .C(clock_1_out), .Reset2(in_4), .O(pc_1_o));
  Multiplexer #(.width(32), .enable("false")) multiplexer_1 (
    .in0({32{1'b0}}), .in1(in_1), .out(multiplexer_1_out), .sel(not_1_out));
  not not_1 (not_1_out, in_3);
  Incrementer4 incrementer4_1 (.in_1(pc_1_o), .out_2(incrementer4_1_out_2));
  // Probe on incrementer4_1_out_2
  // MIPSProgramROM mipsprogramrom_1: pin names not known; wires that end beside it: pc_1_o
  or or_1 (or_1_out, in_5, in_6);
  Register #(.width(32)) register_1 (.D(multiplexer_1_out), .clk(clock_1_out), .Q(out_7));  // open: en, clr
  Register #(.width(32)) register_2 (.D(multiplexer_1_out), .clk(or_1_out), .Q(out_7), .clr(clock_1_out));  // open: en
  Clock clock_1 (.out(clock_1_out));
  decode decode_1 (.I(out_7), .Shamt(decode_1_shamt), .rB(decode_1_rb), .rA(decode_1_ra));
  // RegisterFile registerfile_1: pin names not known; wires that end beside it: registerfile_1_p1, clock_1_out, registerfile_1_p3, registerfile_1_p4, decode_1_ra, decode_1_rb, registerfile_1_p7, registerfile_1_p8
  assign bit_extender_1_out = {{16{out_7[15]}}, out_7[15:0]};  // Bit_Extender bit_extender_1
  IDEX idex_1 (
    .C(clock_1_out), .DA(registerfile_1_p7), .DB(registerfile_1_p8), .DIMM(bit_extender_1_out),
    .Shamt(decode_1_shamt), .QA(idex_1_qa), .QB(idex_1_qb), .QIMM(idex_1_qimm), .Sa(idex_1_sa));
  CtrlIDEX ctrlidex_1 (
    .D(out_7), .C(clock_1_out), .IMM(ctrlidex_1_imm), .Ctrl(ctrlidex_1_ctrl), .Com(ctrlidex_1_com),
    .SU(ctrlidex_1_su), .ALU(ctrlidex_1_alu));
  Multiplexer #(.width(32), .enable("false")) multiplexer_2 (
    .in0(idex_1_qb), .in1(idex_1_qimm), .out(multiplexer_2_out), .sel(ctrlidex_1_imm));
  Forward forward_1 (
    .IDEXRt(decode_1_rb), .IDEXRs(decode_1_ra), .EXMEMRd(ctrlexmem_1_dest), .MEMWBRd(registerfile_1_p4),
    .ForwardB(forward_1_forwardb), .ForwardA(forward_1_forwarda));
  Multiplexer #(.select(2), .width(32), .enable("false")) multiplexer_3 (
    .in0(idex_1_qa), .in1(registerfile_1_p1), .in2(D_q), .in3(D_q), .out(multiplexer_3_out),
    .sel(forward_1_forwarda));
  // Probe on forward_1_forwarda
  // Probe on forward_1_forwardb
  Multiplexer #(.select(2), .width(32), .enable("false")) multiplexer_4 (
    .in0(multiplexer_2_out), .in1(registerfile_1_p1), .in2(D_q), .in3(D_q), .out(multiplexer_4_out),
    .sel(forward_1_forwardb));
  // Mips_ALU mips_alu_1: pin names not known; wires that end beside it: multiplexer_3_out, multiplexer_4_out, ctrlidex_1_alu, idex_1_sa, mips_alu_1_p5
  compare compare_1 (.A(multiplexer_3_out), .B(multiplexer_4_out), .SU(ctrlidex_1_su), .O(compare_1_o));
  Multiplexer #(.width(32), .enable("false")) multiplexer_5 (
    .in0(mips_alu_1_p5), .in1(compare_1_o), .out(multiplexer_5_out), .sel(ctrlidex_1_com));
  Register #(.width(32)) D (.D(multiplexer_5_out), .clk(clock_1_out), .Q(D_q));  // open: en, clr
  CtrlEXMEM ctrlexmem_1 (.D(ctrlidex_1_ctrl), .C(clock_1_out), .Q(ctrlexmem_1_q), .dest(ctrlexmem_1_dest));
  Register #(.width(32)) D_2 (.D(D_q), .clk(clock_1_out), .Q(registerfile_1_p1));  // open: en, clr
  CtrlMEMWB ctrlmemwb_1 (.D(ctrlexmem_1_q), .C(clock_1_out), .dest(registerfile_1_p4), .WE(registerfile_1_p3));

  // Notes on the sheet:
  //   contents of mipsprogramrom_1 (hex, n*v repeats v):
  //   ADDIU $t1, $0, 5 ADDIU $t2, $0, 10 BNE $t6, $0, 0 #Should do nothing, used to make sure no
  //   #forwarded add instructions work SLL $t0, $t0, 0# Another delay instruction SRL $t2, $t2, 2 SLL $t2,
  //   $t2, 2 ADDU $t3, $t1, $t2
endmodule

module Incrementer4 (
  input  [31:0] in_1,
  output [31:0] out_2
);

  // Incrementer #(.width(30)) incrementer_1: pin names not known; wires that end beside it: in_1[31:2], out_2[31:2]

  assign out_2[1:0] = in_1[1:0];
endmodule

module PC (
  input  [31:0] I,
  input  Reset,
  input  C,
  input  Reset2,
  output [31:0] O
);

  wire not_1_out, or_1_out;
  wire [31:0] multiplexer_1_out;

  Multiplexer #(.width(32), .enable("false")) multiplexer_1 (
    .in0({32{1'b0}}), .in1(I), .out(multiplexer_1_out), .sel(not_1_out));
  not not_1 (not_1_out, Reset);
  or or_1 (or_1_out, C, Reset2);
  Register #(.width(32)) register_1 (.D(multiplexer_1_out), .clk(or_1_out), .Q(O));  // open: en, clr
endmodule

module IDEX (
  input  C,
  input  [31:0] DA,
  input  [31:0] DB,
  input  [31:0] DIMM,
  input  [4:0] Shamt,
  output [31:0] QA,
  output [31:0] QB,
  output [31:0] QIMM,
  output [4:0] Sa
);

  Register #(.width(32)) register_1 (.D(DA), .clk(C), .Q(QA));  // open: en, clr
  Register #(.width(5)) register_2 (.D(Shamt), .clk(C), .Q(Sa));  // open: en, clr
  Register #(.width(32)) register_3 (.D(DB), .clk(C), .Q(QB));  // open: en, clr
  Register #(.width(32)) register_4 (.D(DIMM), .clk(C), .Q(QIMM));  // open: en, clr
endmodule

module CtrlIDEX (
  input  [31:0] D,
  input  C,
  output IMM,
  output [31:0] Ctrl,
  output Com,
  output SU,
  output [3:0] ALU
);

  wire and_1_out, and_2_out, and_3_out, and_4_out, and_5_out, and_6_out, and_7_out, and_8_out, and_9_out,
       and_10_out, and_11_out, and_12_out, not_1_out, not_2_out, not_3_out, not_4_out, not_5_out, not_6_out,
       not_7_out, not_8_out, not_9_out, not_10_out, not_11_out, not_12_out, not_13_out, not_14_out,
       not_15_out, not_16_out, not_17_out, not_18_out;

  Register #(.width(32)) register_1 (.D(D), .clk(C), .Q(Ctrl));  // open: en, clr
  not not_1 (not_1_out, Ctrl[27]);
  not not_2 (not_2_out, Ctrl[29]);
  and and_1 (and_1_out, Ctrl[31], Ctrl[26]);
  not not_3 (not_3_out, Ctrl[31]);
  not not_4 (not_4_out, Ctrl[29]);
  not not_5 (not_5_out, Ctrl[31]);
  not not_6 (not_6_out, Ctrl[30]);
  not not_7 (not_7_out, Ctrl[28]);
  not not_8 (not_8_out, Ctrl[31]);
  not not_9 (not_9_out, Ctrl[30]);
  not not_10 (not_10_out, Ctrl[28]);
  not not_11 (not_11_out, Ctrl[31]);
  not not_12 (not_12_out, Ctrl[30]);
  not not_13 (not_13_out, Ctrl[27]);
  not not_14 (not_14_out, Ctrl[31]);
  not not_15 (not_15_out, Ctrl[30]);
  not not_16 (not_16_out, Ctrl[26]);
  not not_17 (not_17_out, Ctrl[30]);
  not not_18 (not_18_out, Ctrl[28]);
  and and_2 (and_2_out, Ctrl[29], not_1_out);
  and and_3 (and_3_out, Ctrl[29], Ctrl[28]);
  and and_4 (and_4_out, Ctrl[31], Ctrl[28]);
  and and_5 (and_5_out, not_2_out, Ctrl[27]);
  and and_6 (and_6_out, Ctrl[29], Ctrl[28]);
  or or_1 (ALU[1], Ctrl[29], and_1_out);
  and and_7 (and_7_out, not_3_out, not_4_out, Ctrl[26]);
  and and_8 (and_8_out, Ctrl[29], Ctrl[28]);
  and and_9 (and_9_out, not_5_out, not_6_out, Ctrl[29], not_7_out, Ctrl[26]);
  and and_10 (and_10_out, not_8_out, not_9_out, Ctrl[29], not_10_out, Ctrl[27]);
  and and_11 (and_11_out, not_11_out, not_12_out, Ctrl[29], Ctrl[28], not_13_out);
  and and_12 (and_12_out, not_14_out, not_15_out, Ctrl[29], Ctrl[28], not_16_out);
  and and_13 (Com, not_17_out, Ctrl[29], not_18_out, Ctrl[27]);
  and and_14 (SU, ~Ctrl[30], Ctrl[29], ~Ctrl[28], Ctrl[27], Ctrl[26]);  // AND_Gate
  or or_2 (ALU[3], and_2_out, and_3_out, and_4_out);
  or or_3 (ALU[2], and_5_out, and_6_out);
  or or_4 (ALU[0], and_7_out, and_8_out);
  or or_5 (IMM, and_9_out, and_10_out, and_11_out, and_12_out);
endmodule

module CtrlMEMWB (
  input  [31:0] D,
  input  C,
  output [4:0] dest,
  output WE
);

  wire and_1_out, and_2_out, and_3_out, and_4_out, and_5_out, and_6_out, and_7_out, and_8_out, and_9_out,
       not_1_out, not_2_out, not_3_out, not_4_out, not_5_out, not_6_out, not_7_out, not_8_out, not_9_out,
       not_10_out, not_11_out, not_12_out, not_13_out, not_14_out, not_15_out, not_16_out, not_17_out,
       not_18_out, not_19_out, not_20_out, not_21_out, not_22_out, not_23_out, not_24_out, not_25_out,
       not_26_out, not_27_out, or_1_out, or_2_out;
  wire [31:0] register_1_q;

  Register #(.width(32)) register_1 (.D(D), .clk(C), .Q(register_1_q));  // open: en, clr
  not not_1 (not_1_out, register_1_q[5]);
  not not_2 (not_2_out, register_1_q[4]);
  not not_3 (not_3_out, register_1_q[3]);
  not not_4 (not_4_out, register_1_q[0]);
  not not_5 (not_5_out, register_1_q[5]);
  not not_6 (not_6_out, register_1_q[4]);
  not not_7 (not_7_out, register_1_q[3]);
  not not_8 (not_8_out, register_1_q[5]);
  not not_9 (not_9_out, register_1_q[4]);
  not not_10 (not_10_out, register_1_q[2]);
  not not_11 (not_11_out, register_1_q[4]);
  not not_12 (not_12_out, register_1_q[3]);
  not not_13 (not_13_out, register_1_q[0]);
  not not_14 (not_14_out, register_1_q[4]);
  not not_15 (not_15_out, register_1_q[3]);
  not not_16 (not_16_out, register_1_q[31]);
  not not_17 (not_17_out, register_1_q[30]);
  not not_18 (not_18_out, register_1_q[28]);
  not not_19 (not_19_out, register_1_q[31]);
  not not_20 (not_20_out, register_1_q[30]);
  not not_21 (not_21_out, register_1_q[28]);
  not not_22 (not_22_out, register_1_q[31]);
  not not_23 (not_23_out, register_1_q[30]);
  not not_24 (not_24_out, register_1_q[27]);
  not not_25 (not_25_out, register_1_q[31]);
  not not_26 (not_26_out, register_1_q[30]);
  not not_27 (not_27_out, register_1_q[26]);
  and and_1 (and_1_out, not_1_out, not_2_out, not_3_out, not_4_out);
  and and_2 (and_2_out, not_5_out, not_6_out, not_7_out, register_1_q[1]);
  and and_3 (and_3_out, not_8_out, not_9_out, not_10_out, register_1_q[1]);
  and and_4 (and_4_out, not_11_out, not_12_out, register_1_q[2], not_13_out);
  and and_5 (and_5_out, register_1_q[5], not_14_out, not_15_out, register_1_q[0]);
  and and_6 (and_6_out, not_16_out, not_17_out, register_1_q[29], not_18_out, register_1_q[26]);
  and and_7 (and_7_out, not_19_out, not_20_out, register_1_q[29], not_21_out, register_1_q[27]);
  and and_8 (and_8_out, not_22_out, not_23_out, register_1_q[29], register_1_q[28], not_24_out);
  and and_9 (and_9_out, not_25_out, not_26_out, register_1_q[29], register_1_q[28], not_27_out);
  or or_1 (or_1_out, and_1_out, and_2_out, and_3_out, and_4_out, and_5_out);
  Multiplexer #(.width(5), .enable("false")) multiplexer_1 (
    .in0(register_1_q[15:11]), .in1(register_1_q[20:16]), .out(dest), .sel(or_2_out));
  or or_2 (or_2_out, and_6_out, and_7_out, and_8_out, and_9_out);
  or or_3 (WE, or_2_out, or_1_out);

  // Notes on the sheet:
  //   dest.
endmodule

module compare (
  input  [31:0] A,
  input  [31:0] B,
  input  SU,
  output [31:0] O
);

  wire comparator_1_eq, comparator_2_eq, multiplexer_1_out;

  Comparator #(.width(32)) comparator_1 (.a(A), .b(B), .eq(comparator_1_eq));  // open: gt, lt
  Comparator #(.width(32), .mode("unsigned")) comparator_2 (.a(A), .b(B), .eq(comparator_2_eq));  // open: gt, lt
  Multiplexer #(.enable("false")) multiplexer_1 (
    .in0(comparator_1_eq), .in1(comparator_2_eq), .out(multiplexer_1_out), .sel(SU));
  assign O = {{31{1'b0}}, multiplexer_1_out};  // Bit_Extender bit_extender_1

  // Notes on the sheet:
  //   signed
  //   unsigned
endmodule

module decode (
  input  [31:0] I,
  output [4:0] Shamt,
  output [4:0] rB,
  output [4:0] rA
);


  assign rA = I[25:21];
  assign rB = I[20:16];
endmodule

module test (
  input  I5,
  input  I4,
  input  I3,
  input  I2,
  input  I1,
  input  I0,
  output O
);

  wire and_1_out, and_2_out, and_3_out, and_4_out, and_5_out, not_1_out, not_2_out, not_3_out, not_4_out,
       not_5_out, not_6_out, not_7_out, not_8_out, not_9_out, not_10_out, not_11_out, not_12_out, not_13_out,
       not_14_out, not_15_out;

  not not_1 (not_1_out, I5);
  not not_2 (not_2_out, I4);
  not not_3 (not_3_out, I3);
  not not_4 (not_4_out, I0);
  not not_5 (not_5_out, I5);
  not not_6 (not_6_out, I4);
  not not_7 (not_7_out, I3);
  not not_8 (not_8_out, I5);
  not not_9 (not_9_out, I4);
  not not_10 (not_10_out, I2);
  not not_11 (not_11_out, I4);
  not not_12 (not_12_out, I3);
  not not_13 (not_13_out, I0);
  not not_14 (not_14_out, I4);
  not not_15 (not_15_out, I3);
  and and_1 (and_1_out, not_1_out, not_2_out, not_3_out, not_4_out);
  and and_2 (and_2_out, not_5_out, not_6_out, not_7_out, I1);
  and and_3 (and_3_out, not_8_out, not_9_out, not_10_out, I1);
  and and_4 (and_4_out, not_11_out, not_12_out, I2, not_13_out);
  and and_5 (and_5_out, I5, not_14_out, not_15_out, I0);
  or or_1 (O, and_1_out, and_2_out, and_3_out, and_4_out, and_5_out);
endmodule

module Forward (
  input  [4:0] IDEXRt,
  input  [4:0] IDEXRs,
  input  [4:0] EXMEMRd,
  input  [4:0] MEMWBRd,
  output [1:0] ForwardB,
  output [1:0] ForwardA
);

  wire nor_1_out, nor_2_out, nor_3_out, nor_4_out, or_1_out, or_2_out;
  wire [4:0] and_1_out, not_1_out, xor_1_out, xor_2_out, xor_3_out, xor_4_out, xor_5_out, xor_6_out;

  assign not_1_out = ~IDEXRs;  // NOT_Gate not_1, 5 bits wide
  assign and_1_out = not_1_out & IDEXRs;  // AND_Gate and_1, 5 bits wide
  assign xor_1_out = MEMWBRd ^ IDEXRs;  // XOR_Gate xor_1, 5 bits wide
  assign xor_2_out = IDEXRt ^ EXMEMRd;  // XOR_Gate xor_2, 5 bits wide
  assign xor_3_out = IDEXRt ^ MEMWBRd;  // XOR_Gate xor_3, 5 bits wide
  assign xor_4_out = EXMEMRd ^ IDEXRs;  // XOR_Gate xor_4, 5 bits wide
  assign xor_5_out = EXMEMRd ^ and_1_out;  // XOR_Gate xor_5, 5 bits wide
  assign xor_6_out = IDEXRs ^ MEMWBRd;  // XOR_Gate xor_6, 5 bits wide
  nor nor_1 (nor_1_out, xor_1_out[0], xor_1_out[1], xor_1_out[2], xor_1_out[3], xor_1_out[4]);
  nor nor_2 (nor_2_out, xor_2_out[0], xor_2_out[1], xor_2_out[2], xor_2_out[3], xor_2_out[4]);
  nor nor_3 (nor_3_out, xor_3_out[0], xor_3_out[1], xor_3_out[2], xor_3_out[3], xor_3_out[4]);
  nor nor_4 (nor_4_out, xor_4_out[0], xor_4_out[1], xor_4_out[2], xor_4_out[3], xor_4_out[4]);
  or or_1 (or_1_out, xor_5_out[0], xor_5_out[1], xor_5_out[2], xor_5_out[3], xor_5_out[4]);
  or or_2 (or_2_out, xor_6_out[0], xor_6_out[1], xor_6_out[2], xor_6_out[3], xor_6_out[4]);
  and and_2 (ForwardA[1], nor_1_out, or_2_out);
  and and_3 (ForwardB[1], or_1_out, nor_2_out);
  and and_4 (ForwardB[0], nor_3_out, or_2_out);
  and and_5 (ForwardA[0], nor_4_out, or_1_out);

  // Notes on the sheet:
  //   Need a 5-bit value of 0000 to make sure Rd isn't $0
endmodule

module CtrlEXMEM (
  input  [31:0] D,
  input  C,
  output [31:0] Q,
  output [4:0] dest
);

  wire and_1_out, and_2_out, and_3_out, and_4_out, not_1_out, not_2_out, not_3_out, not_4_out, not_5_out,
       not_6_out, not_7_out, not_8_out, not_9_out, not_10_out, not_11_out, not_12_out, or_1_out;

  Register #(.width(32)) register_1 (.D(D), .clk(C), .Q(Q));  // open: en, clr
  not not_1 (not_1_out, Q[31]);
  not not_2 (not_2_out, Q[30]);
  not not_3 (not_3_out, Q[28]);
  not not_4 (not_4_out, Q[31]);
  not not_5 (not_5_out, Q[30]);
  not not_6 (not_6_out, Q[28]);
  not not_7 (not_7_out, Q[31]);
  not not_8 (not_8_out, Q[30]);
  not not_9 (not_9_out, Q[27]);
  not not_10 (not_10_out, Q[31]);
  not not_11 (not_11_out, Q[30]);
  not not_12 (not_12_out, Q[26]);
  and and_1 (and_1_out, not_1_out, not_2_out, Q[29], not_3_out, Q[26]);
  and and_2 (and_2_out, not_4_out, not_5_out, Q[29], not_6_out, Q[27]);
  and and_3 (and_3_out, not_7_out, not_8_out, Q[29], Q[28], not_9_out);
  and and_4 (and_4_out, not_10_out, not_11_out, Q[29], Q[28], not_12_out);
  Multiplexer #(.width(5), .enable("false")) multiplexer_1 (.in0(Q[15:11]), .in1(Q[20:16]), .out(dest), .sel(or_1_out));
  or or_1 (or_1_out, and_1_out, and_2_out, and_3_out, and_4_out);

  // Notes on the sheet:
  //   dest.
endmodule
